# Fritzing sketch HC-SR501-Pi (saved by Fritzing 0.9.3b)
circuit board: 8.46667cm x 5.64444cm
breadboards: 1

parts:
  LED1 = smd LED [color="Red (633nm)" package="1206 [SMD]"]
  Raspberry_Pi1 = Raspberry Pi B+
  Header = Header 3 [package=molex-1x3_lock]
  R1 = Resistor [tolerance=±5% resistance=220 package="1206 [SMD]"]

nets (from the breadboard view):
  N1: LED1.cathode, Raspberry_Pi1.GND
  N2: LED1.anode, R1.Pin_1
  N3: Raspberry_Pi1.GPIO15, R1.Pin_0
  N4: Raspberry_Pi1.GPIO14, Header.2
  N5: Raspberry_Pi1.5V, Header.3

notes:
  Smart Home Monitor
  Andrew Liauba
