# Fritzing sketch HC-SR501-Pi_HeaderDesign (saved by Fritzing 0.9.3b)
circuit board: 4.08053cm x 2.33911cm
breadboards: 1

parts:
  Header = Header 3 [package=molex-1x3_lock]
  LED1 = LED - 3mm [color="Red (633nm)" package="3 mm [THT]"]
  R1 = Resistor [tolerance=±5% resistance=220 package=THT]
  J1 = male pin header, 6 pins [form="♂ (male)"]

nets:
  N1: Header.1, J1.pin6
  N2: Header.2, J1.pin4
  N3: Header.3, J1.pin5
  N4: LED1.cathode, R1.Pin_1
  N5: LED1.anode, J1.pin1
  N6: R1.Pin_0, J1.pin3

notes:
  Smart Home Monitor
  Andrew Liauba
